# Fritzing sketch sch1 (saved by Fritzing 0.9.3b)
breadboards: 1

parts:
  Launchpad1 = TI Launchpad MSP430G2
  Componente1 = RFID-RC522-v2
  U1 = ESP8266 WiFi Module [part_number=ESP8266]

nets:
  N1: Launchpad1.p8, Componente1.SDA
  N2: Launchpad1.p7, Componente1.SCK
  N3: Launchpad1.p4, U1.TXD
  N4: Launchpad1.p3, U1.RXD
  3.3V: Launchpad1.p1, Componente1.3.3V, U1.VCC, U1.CH_PD
  N5: Launchpad1.p14, Componente1.MISO
  N6: Launchpad1.p15, Componente1.MOSI
  GND: Launchpad1.p20, U1.RST, U1.GND

custom parts:
  RFID-RC522-v2: A simple China made RFID-RC522 Reader; do check the pin labels, as this is a MFRC522 based clone.
  ESP8266 WiFi Module: Generic WiFi Module based on the ESP8266 with onboard PCB antenna and UART communications
